// Logisim project lab_advanced.circ as structural Verilog: 4 circuits, main circuit main
module main (
  input  [15:0] in_1,
  input  [3:0] in_2,
  output [15:0] out_3
);

  rotr rotr_1 (.A(in_1), .B(in_2), .Out(out_3));
endmodule

module Ex4 (
  input  [7:0] In,
  output Out1,
  output [7:0] Out2
);

  not not_1 (Out2[7], In[7]);
  and and_1 (Out1, In[0], In[7]);

  assign Out2[6:0] = In[6:0];

  // Other names for the same wires on the sheet: mid_bits[5:0] = In[6:1]
endmodule

module rotr (
  input  [15:0] A,
  input  [3:0] B,
  output [15:0] Out
);

  wire clock_1_out, comparator_1_eq, comparator_2_eq, not_1_out, not_2_out, register_3_q;
  wire [3:0] adder_1_out, register_2_q, subtractor_1_out;
  wire [15:0] multiplexer_1_out, n16_bit_single_shift_1_out;

  _16_bit_single_shift u_16_bit_single_shift_1 (.In(Out), .Out(n16_bit_single_shift_1_out));
  Multiplexer #(.width(16)) multiplexer_1 (
    .in0(n16_bit_single_shift_1_out), .in1(A), .out(multiplexer_1_out), .sel(comparator_1_eq));  // open: en
  Comparator #(.width(4)) comparator_1 (.a(4'b0001), .b(register_2_q), .eq(comparator_1_eq));  // open: gt, lt
  Adder #(.width(4)) adder_1 (.a(register_2_q), .b(4'b0001), .out(adder_1_out));  // open: cin, cout
  Clock clock_1 (.out(clock_1_out));
  Register #(.width(16)) register_1 (.D(multiplexer_1_out), .en(not_1_out), .Q(Out), .clk(clock_1_out));  // open: clr
  Register #(.width(4)) register_2 (.D(adder_1_out), .Q(register_2_q), .clk(clock_1_out));  // open: en, clr
  not not_1 (not_1_out, register_3_q);
  Subtractor #(.width(4)) subtractor_1 (.a(register_2_q), .b(4'b0001), .out(subtractor_1_out));  // open: bin, bout
  Register #(.width(1)) register_3 (.D(1'b1), .Q(register_3_q), .clk(not_2_out));  // open: en, clr
  Comparator #(.width(4), .mode("unsigned")) comparator_2 (
    .a(subtractor_1_out), .b(B), .eq(comparator_2_eq));  // open: gt, lt
  not not_2 (not_2_out, comparator_2_eq);
endmodule

module _16_bit_single_shift (
  input  [15:0] In,
  output [15:0] Out
);


  assign Out = {In[0], In[15:1]};
endmodule
