// Logisim project lab_main.circ as structural Verilog: 7 circuits, main circuit main
module main (
);

  AddMachine addmachine_1 ();  // open: out_1, out_2
endmodule

module NAND (
  input  In_0,
  input  In_1,
  output Out
);

  wire and_1_out;

  and and_1 (and_1_out, In_0, In_1);
  not not_1 (Out, and_1_out);
endmodule

module NOR (
  input  In_0,
  input  In_1,
  output Out
);

  wire or_1_out;

  or or_1 (or_1_out, In_0, In_1);
  not not_1 (Out, or_1_out);
endmodule

module XOR (
  input  In_0,
  input  In_1,
  output Out
);

  wire and_1_out, not_1_out, or_1_out;

  and and_1 (and_1_out, In_0, In_1);
  or or_1 (or_1_out, In_1, In_0);
  not not_1 (not_1_out, and_1_out);
  and and_2 (Out, not_1_out, or_1_out);
endmodule

module _2_to_1_MUX (
  input  In_0,
  input  Select,
  input  In_1,
  output Out
);

  wire and_1_out, and_2_out, not_1_out;

  not not_1 (not_1_out, Select);
  and and_1 (and_1_out, In_0, not_1_out);
  and and_2 (and_2_out, Select, In_1);
  or or_1 (Out, and_1_out, and_2_out);
endmodule

module _4_to_1_MUX (
  input  In_0,
  input  Select_1,
  input  In_1,
  input  In_2,
  input  Select_0,
  input  In_3,
  output Out
);

  wire and_1_out, and_2_out, and_3_out, and_4_out, not_1_out, not_2_out;

  not not_1 (not_1_out, Select_1);
  not not_2 (not_2_out, Select_0);
  and and_1 (and_1_out, In_0, not_1_out, not_2_out);
  and and_2 (and_2_out, not_1_out, In_1, Select_0);
  and and_3 (and_3_out, Select_1, In_2, not_2_out);
  and and_4 (and_4_out, Select_1, Select_0, In_3);
  or or_1 (Out, and_1_out, and_2_out, and_3_out, and_4_out);
endmodule

module AddMachine (
  output [7:0] out_1,
  output [7:0] out_2
);

  wire clock_1_out;

  Adder adder_1 (.a(out_1), .b(8'h1), .out(out_2));  // open: cin, cout
  Clock clock_1 (.out(clock_1_out));
  Register register_1 (.D(out_2), .Q(out_1), .clk(clock_1_out));  // open: en, clr
endmodule
